# Fritzing sketch IR-RGB-remote-v1-dot-board-v3_flat_design (saved by Fritzing 0.9.3b)
perfboards: 1

parts:
  Part2 = Arduino Nano (Rev3.0)
  TSOP48 = TSOP312.., 314.. [package=THT]
  J1 = Dagu DGServo 9g header connector (female) [package=THT]
  Q8 = Basic FET N-Channel [package="TO220 [THT]"]
  R29 = Resistor [tolerance=±5% resistance=10k package=THT]
  R30 = Resistor [tolerance=±20% resistance=10k package=THT]
  R31 = Resistor [tolerance=±5% resistance=10k package=THT]
  Q9 = Basic FET N-Channel [package="TO220 [THT]"]
  R32 = Resistor [tolerance=±5% resistance=10k package=THT]
  Q10 = Basic FET N-Channel [package="TO220 [THT]"]
  R33 = Resistor [tolerance=±20% resistance=10k package=THT]
  R34 = Resistor [tolerance=±20% resistance=10k package=THT]
  J3 = Camdenboss CTB0158-2 [part_number=CTB0158-2 package=THT]
  J4 = female pin header, 2 pins [form="♀ (female)"]
  C3 = Capacitor Polarized [package=cpol-radial-100uf-25v]
  J7 = Dagu DGServo 9g header connector (female) [package=THT]

nets:
  N1: Part2.GND, J1.pulse, Q8.source, R29.Pin_1, R31.Pin_1, Q9.source, J3.pin2, J7.pulse
  N2: Part2.D2, J1.gnd
  N3: Part2.D9, R34.Pin_1
  N4: Part2.D10, R33.Pin_1
  N5: Part2.D11/MOSI, R30.Pin_1
  N6: Part2.VIN, J3.pin1, J4.pin2
  VCC: Part2.5V, J1.Vcc, J7.Vcc
  N7: Part2.A5, J7.gnd
  N8: TSOP48.GND, C3.-
  N9: TSOP48.Vs, C3.+
  N10: Q8.gate, R29.Pin_0, R30.Pin_0
  N11: R31.Pin_0, Q9.gate, R33.Pin_0
  N12: R32.Pin_0, Q10.gate, R34.Pin_0
  N13: R32.Pin_1, Q10.source

custom parts:
  TSOP312.., 314..: The TSOP312.., TSOP314.. series are miniaturized receivers for infrared remote control systems. A PIN diode and a preamplifier are assembled on a lead frame, the epoxy package acts as an IR filter. The demodulated output signal can be directly decoded by a microprocessor. The TSOP312.. is compatible with all common IR remote control data formats. The TSOP314.. is optimized to suppress almost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
